# Fritzing sketch Hardwareopstelling (saved by Fritzing 0.8.7b)
breadboards: 1

parts:
  S1 = Pushbutton [package="[THT]"]
  S2 = Pushbutton [package="[THT]"]
  S3 = Pushbutton [package="[THT]"]
  S4 = Pushbutton [package="[THT]"]
  LED1 = LED - 5mm [color="Red (633nm)" package="5 mm [THT]"]
  LED2 = LED - 5mm [color="Red (633nm)" package="5 mm [THT]"]
  LED3 = LED - 5mm [color="Red (633nm)" package="5 mm [THT]"]
  LED4 = LED - 5mm [color="Red (633nm)" package="5 mm [THT]"]
  LED5 = LED - 5mm [color="Red (633nm)" package="5 mm [THT]"]
  LED6 = LED - 5mm [color="Red (633nm)" package="5 mm [THT]"]
  J1 = Piezo Speaker
  U1 = 74HC595 [package="DIP16 [THT]"]  # not connected
  Onderdeel1 = Arduino Uno (Rev3)
  R1 = Resistor [tolerance=±5% resistance=220 package=THT]
  R2 = Resistor [tolerance=±5% resistance=220 package=THT]
  R3 = Resistor [tolerance=±5% resistance=220 package=THT]
  R4 = Resistor [tolerance=±5% resistance=220 package=THT]
  R5 = Resistor [tolerance=±5% resistance=220 package=THT]
  R6 = Resistor [tolerance=±5% resistance=220 package=THT]
  R7 = Resistor [tolerance=±5% resistance=220 package="1206 [SMD]"]
  R8 = Resistor [tolerance=±5% resistance=220 package="1206 [SMD]"]
  R9 = Resistor [tolerance=±5% resistance=220 package="1206 [SMD]"]
  R10 = Resistor [tolerance=±5% resistance=220 package="1206 [SMD]"]
  R12 = Resistor [tolerance=±5% resistance=220 package="0603 [SMD]"]  # not connected
  R13 = Resistor [tolerance=±5% resistance=220 package="0603 [SMD]"]  # not connected
  R14 = Resistor [tolerance=±5% resistance=220 package="0603 [SMD]"]  # not connected
  R15 = Resistor [tolerance=±5% resistance=220 package="0603 [SMD]"]  # not connected
  R16 = Resistor [tolerance=±5% resistance=220 package="0603 [SMD]"]  # not connected
  R17 = Resistor [tolerance=±5% resistance=220 package="0603 [SMD]"]  # not connected
  7_Segment1 = 7 Segment Display  # not connected
  R18 = Resistor [tolerance=±5% resistance=220 package="0603 [SMD]"]  # not connected
  J2 = Basic Servo

nets:
  GND: S1.Pin_1, S1.Pin_2, S2.Pin_1, S2.Pin_2, S3.Pin_1, S3.Pin_2, S4.Pin_1, S4.Pin_2, J1.pin1, Onderdeel1.GND, R1.Pin_0, R3.Pin_0, R4.Pin_1, R5.Pin_0, R6.Pin_0, J2.gnd
  N1: S1.Pin_3, S1.Pin_4, Onderdeel1.D5_PWM, R10.Pin_0
  N2: S2.Pin_3, S2.Pin_4, Onderdeel1.D6_PWM, R8.Pin_0
  N3: S3.Pin_3, S3.Pin_4, Onderdeel1.D9_PWM, R7.Pin_0
  N4: S4.Pin_3, S4.Pin_4, Onderdeel1.D10_PWM/SS, R9.Pin_0
  N5: LED1.cathode, Onderdeel1.D13/SCK
  N6: LED1.anode, R5.Pin_1
  N7: LED2.cathode, Onderdeel1.D8
  N8: LED2.anode, R6.Pin_1
  N9: LED3.cathode, Onderdeel1.D7
  N10: LED3.anode, R4.Pin_0
  N11: LED4.cathode, Onderdeel1.D2
  N12: LED4.anode, R1.Pin_1
  N13: LED5.cathode, Onderdeel1.D3_PWM
  N14: LED5.anode, R2.Pin_1
  N15: LED6.cathode, Onderdeel1.D4
  N16: LED6.anode, R3.Pin_1
  N17: J1.pin2, Onderdeel1.D12/MISO
  N18: Onderdeel1.D11_PWM/MOSI, J2.pulse
  5V: Onderdeel1.5V, R7.Pin_1, R8.Pin_1, R9.Pin_1, R10.Pin_1, J2.vcc
